# Fritzing sketch ObstacleCar_1_Bridge_4wd (saved by Fritzing 0.9.4)

parts:
  Part1 = Arduino Uno (Rev3)
  S2 = H-Bridge with L298N
  HC-SR04_Sensor_1 = HC-SR04 Ultrasonic Distance Sensor  # not connected
  M5 = DC Motor
  M6 = DC Motor
  BAT5 = BC9VPC [package=bc9vpc]
  M7 = DC Motor
  M8 = DC Motor

nets:
  GND: Part1.GND, S2.GND, BAT5.V-
  N1: Part1.D2, S2.IN4
  N2: Part1.D3_PWM, S2.ENB
  N3: Part1.D4, S2.IN3
  N4: Part1.D5_PWM, S2.IN2
  N5: Part1.D6_PWM, S2.ENA
  N6: Part1.D7, S2.IN1
  5V: Part1.5V, S2.5V
  N7: S2.12V, BAT5.V+
  N8: S2.M1-01, M7.pin_2, M8.pin_2
  N9: S2.M1-02, M7.pin_1, M8.pin_1
  N10: S2.M2-01, M5.pin_2, M6.pin_2
  N11: S2.M2-02, M5.pin_1, M6.pin_1

notes:
  TODO:
  5V Out of the H-Bridge is powering Arduino

custom parts:
  H-Bridge with L298N: h-bridge
